# Fritzing sketch autoblinds (saved by Fritzing 0.9.3b)
circuit board: 4.84928cm x 3.65957cm
breadboards: 1

parts:
  Trinket_Pro_5V = Adafruit Pro Trinket 5V 16MHz [part_number="Adafruit #2000"]
  S1 = Momentary Switch [package=ksa_sealed_tac_switch]
  R1 = Resistor [tolerance=±5% resistance=10k package="1206 [SMD]"]
  J1 = Basic Servo
  R2 = Resistor [tolerance=±5% resistance=10k package="1206 [SMD]"]
  R3 = Resistor [tolerance=±5% resistance=10k package="1206 [SMD]"]
  J2 = female pin header, 2 pins [form="♀ (female)"]
  U1 = Monoprice Z Wave Curtain Module

nets:
  GND: Trinket_Pro_5V.GND, R1.Pin_0, J1.gnd, U1.GND
  VCC: Trinket_Pro_5V.VBUS, J1.vcc, R2.Pin_1, R3.Pin_1, U1.Vcc
  N1: Trinket_Pro_5V.RXD, J1.pulse
  N2: Trinket_Pro_5V.+5V, S1.1, S1.2, J2.pin1
  N3: Trinket_Pro_5V.D11, R2.Pin_0, U1.open
  N4: Trinket_Pro_5V.D12, R3.Pin_0, U1.close
  N5: Trinket_Pro_5V.A1, S1.3, S1.4, R1.Pin_1, J2.pin2

notes:
  Automated Blinds
  Automatic Blinds ESD, Trae Blain Design, -

custom parts:
  Adafruit Pro Trinket 5V 16MHz: Trinket's got a big sister in town - the Pro Trinket 5V! Pro Trinket combines everything you love about Trinket with the familiarity of the common core Arduino chip, the ATmega328. It's like an Arduino Pro Mini with more pins and USB tossed in, so delicious. Trinket's a year old now, and while its been great to see tons of tiny projects, sometimes you just need more pins, more FLASH, and more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
  Monoprice Z Wave Curtain Module: Monoprice's Z Wave Curtain Module http://www.monoprice.com/product?p_id=11992
